# Fritzing sketch Untitled Sketch (saved by Fritzing 0.9.3b)
breadboards: 1

parts:
  U1 = LM 358 Dual Op-Amp [package="DIP8 [THT]"]
  R1 = Resistor [tolerance=±5% resistance=10k package=THT]
  R2 = Resistor [tolerance=±5% resistance=10k package=THT]
  J1 = Basic Force Sensing Resistor (FSR) [package=THT]
  J2 = Basic Force Sensing Resistor (FSR) [package=THT]
  Raspberry_Pi_1 = Raspberry Pi 3 [part_number=RPI-3-V1.2]

nets:
  N1: U1.connector0, Raspberry_Pi_1.GPIO10
  N2: U1.connector1, Raspberry_Pi_1.GPIO9
  N3: U1.connector2, Raspberry_Pi_1.GPIO11
  N4: U1.connector3, J1.pin_0, J2.pin_1, Raspberry_Pi_1.3v3
  N5: U1.connector4, Raspberry_Pi_1.GPIO8
  N6: U1.connector5, R1.Pin_1, J1.pin_1
  N7: U1.connector6, R2.Pin_1, J2.pin_0
  N8: U1.connector7, R1.Pin_0, R2.Pin_0, Raspberry_Pi_1.GND
